# Fritzing sketch I2CServiceModule (saved by Fritzing 0.9.10b)
circuit board: 5.19999cm x 5.19999cm
breadboards: 1

parts:
  MCP23008 = IC, DIP package, 18 pins [chip_label=IC]
  I2C = female pin header, 4 pins [form="♀ (female)"]
  battmon = female pin header, 1 pin [form="♀ (female)"]
  NBJT2 = NPN-Transistor [part_number=2N2222 package="TO92 [THT]"]
  NBJT3 = NPN-Transistor [part_number=2N2222 package="TO92 [THT]"]
  NBJT1 = NPN-Transistor [part_number=2N2222 package="TO92 [THT]"]
  D1 = Rectifier Diode [part_number=1N4001 package="300 mil [THT]"]
  D2 = Rectifier Diode [part_number=1N4001 package="300 mil [THT]"]
  R1 = Resistor [tolerance=±5% resistance=15k power=0.25 package=THT]
  R4 = Resistor [tolerance=±5% power=0.25 resistance=15k package=THT]
  R2 = Resistor [tolerance=±5% resistance=4.7k power=0.25 package=THT]
  R3 = Resistor [tolerance=±5% resistance=3.0k power=0.25 package=THT]
  R8 = Resistor [tolerance=±5% power=0.25 resistance=15k package=THT]
  R5 = Resistor [tolerance=±5% resistance=15k power=0.25 package=THT]
  R7 = Resistor [tolerance=±5% resistance=3.0k power=0.25 package=THT]
  R6 = Resistor [tolerance=±5% resistance=4.7k power=0.25 package=THT]
  R11 = Resistor [tolerance=±5% resistance=3.0k power=0.25 package=THT]
  R9 = Resistor [tolerance=±5% resistance=15k power=0.25 package=THT]
  R10 = Resistor [tolerance=±5% resistance=4.7k power=0.25 package=THT]
  PFET1 = mystery part, 3 pins [chip_label=? part_number=FQU8P10]
  R14 = Resistor [tolerance=±5% power=0.25 resistance=74k package=THT]
  R13 = Resistor [tolerance=±5% power=0.25 resistance=10k package=THT]
  R15 = Resistor [tolerance=±5% power=0.25 resistance=10k package=THT]
  R16 = Resistor [tolerance=±5% power=0.25 resistance=10k package=THT]
  Adr = female pin header, 3 pins [form="♀ (female)"]
  PFET2 = mystery part, 3 pins [chip_label=? part_number=FQU8P10]
  PFET3 = mystery part, 3 pins [chip_label=? part_number=FQU8P10]
  Ch1 = XT-30 [package=THT]
  Ch2 = XT-30 [package=THT]
  3S_LiPo = XT-30 [package=THT]

nets:
  N1: MCP23008.pin1, I2C.pin4, R15.Pin_0
  N2: MCP23008.pin2, I2C.pin3, R16.Pin_0
  N3: MCP23008.pin3, MCP23008.pin9, I2C.pin1, NBJT2.E, NBJT3.E, NBJT1.E, R2.Pin_0, R6.Pin_0, R10.Pin_0, R13.Pin_0, Adr.pin1, Ch1.pin2, Ch2.pin2, 3S_LiPo.pin2
  N4: MCP23008.pin4, Adr.pin2
  N5: MCP23008.pin5, MCP23008.pin6, MCP23008.pin18, I2C.pin2, R15.Pin_1, R16.Pin_1, Adr.pin3
  N6: MCP23008.pin10, D1.anode, R4.Pin_1
  N7: MCP23008.pin11, R3.Pin_0
  N8: MCP23008.pin12, R4.Pin_0
  N9: MCP23008.pin13, battmon.pin1, R14.Pin_0, R13.Pin_1
  N10: MCP23008.pin14, R8.Pin_0
  N11: MCP23008.pin15, R11.Pin_0
  N12: MCP23008.pin16, R7.Pin_0
  N13: MCP23008.pin17, D2.anode, R8.Pin_1
  N14: NBJT2.B, R7.Pin_1, R6.Pin_1
  N15: NBJT2.C, R5.Pin_1, PFET2.pin1
  N16: NBJT3.B, R11.Pin_1, R10.Pin_1
  N17: NBJT3.C, R9.Pin_1, PFET3.pin1
  N18: NBJT1.B, R2.Pin_1, R3.Pin_1
  N19: NBJT1.C, R1.Pin_1, PFET1.pin1
  N20: D1.cathode, PFET1.pin2, Ch1.pin1
  N21: D2.cathode, PFET2.pin2, Ch2.pin1
  N22: R1.Pin_0, R5.Pin_0, PFET1.pin3, PFET2.pin3, PFET3.pin2
  N23: R9.Pin_0, R14.Pin_1, PFET3.pin3, 3S_LiPo.pin1

notes:
  Tst 1 2
  Sn 2  7
  Ch 2  6
  Ch 1  1
  Tst 2 4
  Sn 1  0
  G 3V SDA SCL
  I2C Service Module
  0x23  0x21
  BattMon 3
  Mike Loman 2025
  PwrOn  5
  Assy notes: Move R15 & R16 to btm & lay flat. Move Ch1 & 3S LiPo to btm. Make 2026 version. Move Adr hdr to btm. Poss. breakout Adr0 as well as Adr1

custom parts:
  XT-30: Screw terminal with 2 pins
